# Fritzing sketch lunchbeat0 (saved by Fritzing 0.8.3b)
perfboards: 7

parts:
  R2 = Resistor [tolerance=±5% resistance=100k package=THT]
  U2 = 74HC595 [package="DIP16 [THT]"]
  U3 = LM 358 Dual Op-Amp [package="DIP8 [THT]"]
  U1 = atmega328 [package=dip]
  HIHAT = Pushbutton [package="[THT]"]
  SNARE = Pushbutton [package="[THT]"]
  KICK = Pushbutton [package="[THT]"]
  RESET = Pushbutton [package="[THT]"]
  BASS = Pushbutton [package="[THT]"]
  R9 = Resistor [tolerance=±5% resistance=10k package=THT]
  PLAY = Pushbutton [package="[THT]"]
  C2 = Ceramic Capacitor [capacitance=22pF package="100 mil [THT, multilayer]"]
  C1 = Ceramic Capacitor [capacitance=22pF package="100 mil [THT, multilayer]"]
  EDIT = Pushbutton [package="[THT]"]
  R5 = Resistor [tolerance=±5% resistance=100k package=THT]
  R6 = Resistor [tolerance=±5% resistance=100k package=THT]
  R7 = Resistor [tolerance=±5% resistance=100k package=THT]
  R4 = Resistor [tolerance=±5% resistance=100k package=THT]
  R3 = Resistor [tolerance=±5% resistance=100k package=THT]
  R1 = Resistor [tolerance=±5% resistance=100k package=THT]
  R8 = Resistor [tolerance=±5% resistance=100k package=THT]
  J1 = Audio Jack (TRS) 3.5mm [package="PG203J [THT]"]
  C3 = Electrolytic Capacitor [capacitance=10µF package="100 mil [THT, electrolytic]"]
  R26 = Resistor [tolerance=±5% resistance=82 package=THT]
  R25 = Resistor [tolerance=±5% resistance=82 package=THT]
  R24 = Resistor [tolerance=±5% resistance=82 package=THT]
  R23 = Resistor [tolerance=±5% resistance=82 package=THT]
  R22 = Resistor [tolerance=±5% resistance=82 package=THT]
  R27 = Resistor [tolerance=±5% resistance=82 package=THT]
  R21 = Resistor [tolerance=±5% resistance=82 package=THT]
  R20 = Resistor [tolerance=±5% resistance=82 package=THT]
  XTAL1 = Crystal [frequency="16 MHz" package=THT]
  U4 = Voltage Regulator - 5V [package="DPak [SMD]"]
  C5 = Ceramic Capacitor [capacitance=0.1µF package="100 mil [THT, multilayer]"]
  C4 = Ceramic Capacitor [capacitance=47µF package="100 mil [THT, multilayer]"]
  C6 = Electrolytic Capacitor [capacitance=1µF package="100 mil [THT, electrolytic]"]
  D1 = Rectifier Diode [part_number=1N4001 package="300 mil [THT]"]
  Power = Power plug [part_number=PJ-002A]
  LED8 = LED - 3mm [color="Blue (470nm)" package="3 mm [THT]"]
  LED7 = LED - 3mm [color="Blue (470nm)" package="3 mm [THT]"]
  LED6 = LED - 3mm [color="Blue (470nm)" package="3 mm [THT]"]
  LED5 = LED - 3mm [color="Blue (470nm)" package="3 mm [THT]"]
  LED4 = LED - 3mm [color="Blue (470nm)" package="3 mm [THT]"]
  LED3 = LED - 3mm [color="Blue (470nm)" package="3 mm [THT]"]
  LED2 = LED - 3mm [color="Blue (470nm)" package="3 mm [THT]"]
  LED1 = LED - 3mm [color="Blue (470nm)" package="3 mm [THT]"]
  R15_-_KICK = Rotary Potentiometer (Small)
  R16_-_SNARE = Rotary Potentiometer (Small)
  R17_-_HIHAT = Rotary Potentiometer (Small)
  R18_-_BASS = Rotary Potentiometer (Small)
  R19_-_TEMPO = Rotary Potentiometer (Small) [maximum_resistance=10kΩ]

nets:
  N1: R2.Pin_0, U1.D5_(PWM)
  N2: R2.Pin_1, R4.Pin_1, R3.Pin_1, R1.Pin_0
  N3: U2.Q1, LED7.anode
  N4: U2.Q2, LED6.anode
  N5: U2.Q3, LED5.anode
  N6: U2.Q4, LED4.anode
  N7: U2.Q5, LED3.anode
  N8: U2.Q6, LED2.anode
  N9: U2.Q7, LED1.anode
  GND: U2.GND, U2.OE, U3.connector3, U1.GND, HIHAT.Pin_1, HIHAT.Pin_2, SNARE.Pin_1, SNARE.Pin_2, KICK.Pin_1, KICK.Pin_2, RESET.Pin_1, RESET.Pin_2, BASS.Pin_1, BASS.Pin_2, PLAY.Pin_1, PLAY.Pin_2, C2.0, C1.0, EDIT.Pin_3, EDIT.Pin_4, R1.Pin_1, J1.Sleeve, R26.Pin_0, R25.Pin_0, R24.Pin_0, R23.Pin_0, R22.Pin_0, R27.Pin_0, R21.Pin_0, R20.Pin_0, U4.GND, C5.0, C4.0, C6.-, Power.GND, R15_-_KICK.leg1, R16_-_SNARE.leg1, R17_-_HIHAT.leg1, R18_-_BASS.leg1, R19_-_TEMPO.leg1
  5V: U2.MR, U2.VCC, U3.connector7, U1.VCC, U1.AVCC, U1.AREF, R9.Pin_0, U4.output_voltage, C5.1, R15_-_KICK.leg2, R16_-_SNARE.leg2, R17_-_HIHAT.leg2, R18_-_BASS.leg2, R19_-_TEMPO.leg2
  N10: U2.SH_CP, U1.D13
  N11: U2.ST_CP, U1.D10_(PWM)
  N12: U2.DS, U1.D11_(PWM)
  N13: U2.Q0, LED8.anode
  N14: U3.connector0, U3.connector1, C3.+
  N15: U3.connector2, R6.Pin_0, R7.Pin_0, R8.Pin_1
  N16: U1.RESET, RESET.Pin_3, RESET.Pin_4, R9.Pin_1
  N17: U1.D0_(RX), KICK.Pin_3, KICK.Pin_4
  N18: U1.D1_(TX), SNARE.Pin_3, SNARE.Pin_4
  N19: U1.D2, HIHAT.Pin_3, HIHAT.Pin_4
  N20: U1.D3_(PWM), BASS.Pin_3, BASS.Pin_4
  N21: U1.D4, PLAY.Pin_3, PLAY.Pin_4
  N22: U1.XLAT1, C1.1, XTAL1.pin_0
  N23: U1.XLAT2, C2.1, XTAL1.pin_1
  N24: U1.D6_(PWM), R5.Pin_0
  N25: U1.D7, R8.Pin_0
  N26: U1.D8, EDIT.Pin_1, EDIT.Pin_2
  N27: U1.A0, R19_-_TEMPO.wiper
  N28: U1.A1, R18_-_BASS.wiper
  N29: U1.A2, R17_-_HIHAT.wiper
  N30: U1.A3, R16_-_SNARE.wiper
  N31: U1.A4, R15_-_KICK.wiper
  N32: R5.Pin_1, R6.Pin_1, R7.Pin_1, R4.Pin_0, R3.Pin_0
  N33: J1.Ring, J1.Tip, C3.-
  N34: R26.Pin_1, LED7.cathode
  N35: R25.Pin_1, LED6.cathode
  N36: R24.Pin_1, LED5.cathode
  N37: R23.Pin_1, LED4.cathode
  N38: R22.Pin_1, LED3.cathode
  N39: R27.Pin_1, LED8.cathode
  N40: R21.Pin_1, LED2.cathode
  N41: R20.Pin_1, LED1.cathode
  N42: U4.input_voltage, C4.1, C6.+, D1.cathode
  N43: D1.anode, Power.VCC

notes:
  AUDIO OUT
  LEDS AND SHIFT REGISTER
  BRAIN
  POTS
  RESET
  SNARE
  HIHAT
  KICK
  BASS
  PLAY
  EDIT
  POWER
  R2R DAC LADDER
  TEMPO
  LUNCHBEAT
  github.com/antivapor
  forked from buranelectrix
  2013
